// Logisim project 1.circ as structural Verilog
module decoder2_4 (
  input  A1,
  input  A0,
  output y3,
  output y2,
  output y1,
  output y0
);

  wire not_1_out, not_2_out;

  not not_1 (not_1_out, A1);
  not not_2 (not_2_out, A0);
  and and_1 (y3, A1, A0);
  and and_2 (y2, A1, not_2_out);
  and and_3 (y1, not_1_out, A0);
  and and_4 (y0, not_1_out, not_2_out);
endmodule

module decoder3_8 (
  input  A2,
  input  A1,
  input  A0,
  output y7,
  output y6,
  output y5,
  output y4,
  output y3,
  output y2,
  output y1,
  output y0
);

  wire decoder2_4_1_y0, decoder2_4_1_y1, decoder2_4_1_y2, decoder2_4_1_y3, not_1_out;

  decoder2_4 decoder2_4_1 (
    .A1(A1), .A0(A0), .y3(decoder2_4_1_y3), .y2(decoder2_4_1_y2), .y1(decoder2_4_1_y1), .y0(decoder2_4_1_y0));
  not not_1 (not_1_out, A2);
  and and_1 (y7, decoder2_4_1_y3, A2);
  and and_2 (y6, decoder2_4_1_y2, A2);
  and and_3 (y5, decoder2_4_1_y1, A2);
  and and_4 (y4, A2, decoder2_4_1_y0);
  and and_5 (y3, decoder2_4_1_y3, not_1_out);
  and and_6 (y2, decoder2_4_1_y2, not_1_out);
  and and_7 (y1, decoder2_4_1_y1, not_1_out);
  and and_8 (y0, decoder2_4_1_y0, not_1_out);
endmodule

module priority_encode4_2 (
  input  A3,
  input  A2,
  input  A1,
  input  A0,
  output Y1,
  output Y0
);

  wire or_2_out, or_3_out;

  or or_1 (Y1, A3, A2);
  or or_2 (or_2_out, Y1, A1);
  or or_3 (or_3_out, A3, ~A2);  // OR_Gate
  and and_1 (Y0, or_2_out, or_3_out);
endmodule

module D_latch (
  input  WE,
  input  D,
  output Q,
  output nQ
);

  wire and_1_out, and_2_out;

  and and_1 (and_1_out, ~D, WE);  // AND_Gate
  nor nor_1 (Q, and_1_out, nQ);
  and and_2 (and_2_out, WE, D);
  nor nor_2 (nQ, Q, and_2_out);
endmodule

module D_FF (
  input  D,
  input  WE,
  input  clk,
  input  reset,
  output Q
);

  wire and_1_out, and_2_out, and_3_out, and_4_out, d_latch_1_q, or_1_out, or_2_out;

  and and_1 (and_1_out, ~clk, WE);  // AND_Gate
  or or_1 (or_1_out, and_1_out, reset);
  and and_2 (and_2_out, D, ~reset);  // AND_Gate
  D_latch d_latch_1 (.WE(or_1_out), .D(and_2_out), .Q(d_latch_1_q));  // open: nQ
  and and_3 (and_3_out, clk, WE);
  or or_2 (or_2_out, and_3_out, reset);
  and and_4 (and_4_out, d_latch_1_q, ~reset);  // AND_Gate
  D_latch d_latch_2 (.WE(or_2_out), .D(and_4_out), .Q(Q));  // open: nQ
endmodule
